# Fritzing sketch Simon Game (saved by Fritzing 0.8.7b)
breadboards: 1

parts:
  Part1 = Adafruit Feather HUZZAH ESP8266 [part_number="Adafruit #2821"]
  S1 = Momentary Switch [package=ksa_sealed_tac_switch]
  S2 = Momentary Switch [package=ksa_sealed_tac_switch]
  S3 = Momentary Switch [package=ksa_sealed_tac_switch]
  R2 = Resistor [tolerance=±5% resistance=560 package=THT]
  R3 = Resistor [tolerance=±5% resistance=560 package=THT]
  R4 = Resistor [tolerance=±5% resistance=560 package=THT]
  R5 = Resistor [tolerance=±5% resistance=560 package=THT]
  R6 = Resistor [tolerance=±5% resistance=220 package=THT]
  R7 = Resistor [tolerance=±5% resistance=220 package=THT]
  R8 = Resistor [tolerance=±5% resistance=220 package=THT]
  LED3 = LED - 5mm [color="Red (633nm)" package="5 mm [THT]"]
  LED4 = LED - 5mm [color="Green (565nm)" package="5 mm [THT]"]
  J1 = Piezo Speaker
  LED2 = smd LED [color="Blue (525nm)" package="1206 [SMD]"]

nets:
  N1: Part1.GPIO12/MISO, R2.Pin_1
  N2: Part1.GPIO13/MOSI, R3.Pin_1
  N3: Part1.GPIO14/SCK, R4.Pin_1
  N4: Part1.GND, R6.Pin_0, R8.Pin_0, LED3.anode, J1.pin1
  N5: Part1.3.3V, S1.1, S2.1, S3.1
  N6: Part1.GPIO15, S3.4
  N7: Part1.GPIO16, R5.Pin_1
  N8: Part1.GPIO5/SCL, S2.4
  N9: Part1.GPIO4/SDA, S1.4
  N10: S1.3, R8.Pin_1
  N11: S2.3, R7.Pin_1
  N12: S3.3, R6.Pin_1
  N13: R2.Pin_0, LED2.cathode
  N14: R3.Pin_0, LED3.cathode
  N15: R4.Pin_0, LED4.cathode
  N16: R5.Pin_0, J1.pin2

custom parts:
  Adafruit Feather HUZZAH ESP8266: his is the Adafruit Feather HUZZAH ESP8266 - our take on an 'all-in-one' ESP8266 WiFi development board with built in USB and battery charging. Its an ESP8266 WiFi module with all the extras you need, ready to rock! We have other boards in the Feather family, check'em out here. At the Feather HUZZAH's heart is an ESP8266 WiFi microcontroller clocked at 80 MHz and at 3.3V logic. This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
